// Logisim project FINAL_CPU.circ as structural Verilog: 12 circuits, main circuit COMMON_BUS
module CPU (
  input  WRT,
  input  OPT,
  input  clr,
  input  R,
  input  E,
  input  C_in,
  input  in_7,
  input  IL,
  input  TR_id,
  input  TR_inr,
  input  TR_clr,
  input  comE,
  input  E_inp,
  input  LOAD,
  input  D_CLR,
  input  in_16
);

  wire and_1_out, CLK_out, clock_1_out, common_bus_1_p29, common_bus_1_p30, common_bus_1_p31,
       common_bus_1_p34, control_unit_1_ac_clr, control_unit_1_ac_inr, control_unit_1_ac_ld,
       control_unit_1_ar_clr, control_unit_1_ar_inr, control_unit_1_ar_ld, control_unit_1_dr_clr,
       control_unit_1_dr_inr, control_unit_1_dr_ld, control_unit_1_ir_ld, control_unit_1_pc_clr,
       control_unit_1_pc_inr, control_unit_1_pc_ld, not_1_out, or_1_out, SC_clk;
  wire [2:0] control_unit_1_s2s1s0, control_unit_1_selc;
  wire [15:0] AC, DR, IR;

  not not_1 (not_1_out, clr);
  and and_1 (and_1_out, not_1_out, SC_clk);
  or or_1 (or_1_out, in_16, and_1_out);
  D_Flip_Flop d_ff_1 (.D(or_1_out), .clk(CLK_out), .Q(SC_clk));  // open: Qn, preset, reset
  Clock CLK (.out(CLK_out));
  Control_unit control_unit_1 (
    .SC_clr(clr), .ir(IR), .SC_clk(SC_clk), .R(R), .E(E), .DR(DR), .AC(AC), .AR_ld(control_unit_1_ar_ld),
    .AR_clr(control_unit_1_ar_clr), .AR_inr(control_unit_1_ar_inr), .PC_ld(control_unit_1_pc_ld),
    .PC_inr(control_unit_1_pc_inr), .PC_clr(control_unit_1_pc_clr), .S2S1S0(control_unit_1_s2s1s0),
    .DR_ld(control_unit_1_dr_ld), .DR_inr(control_unit_1_dr_inr), .DR_clr(control_unit_1_dr_clr),
    .AC_ld(control_unit_1_ac_ld), .AC_inr(control_unit_1_ac_inr), .AC_clr(control_unit_1_ac_clr),
    .IR_ld(control_unit_1_ir_ld), .selc(control_unit_1_selc));
  Clock #(.phaseOffset(1)) clock_1 (.out(clock_1_out));
  // COMMON_BUS common_bus_1: pin names not known; wires that end beside it: WRT, OPT, control_unit_1_ar_ld, control_unit_1_ar_clr, control_unit_1_ar_inr, control_unit_1_pc_ld, control_unit_1_pc_inr, control_unit_1_pc_clr, control_unit_1_s2s1s0, control_unit_1_dr_ld, control_unit_1_dr_inr, control_unit_1_dr_clr, control_unit_1_ac_ld, control_unit_1_ac_inr, control_unit_1_ac_clr, control_unit_1_ir_ld, control_unit_1_selc, TR_id, TR_inr, TR_clr, comE, E_inp, LOAD, D_CLR, clock_1_out, C_in, in_7, IL, common_bus_1_p29, common_bus_1_p30, common_bus_1_p31, DR, AC, common_bus_1_p34, IR
  // Probe on common_bus_1_p29
  // Probe on common_bus_1_p31
  // Probe on AC
  // Probe on IR
  // Probe on common_bus_1_p30
  // Probe on DR
  // Probe on common_bus_1_p34

  // Other names for the same wires on the sheet: SC_clr = clr
endmodule

module COMMON_BUS (
  input  write,
  input  out_ena,
  input  AR_ld,
  input  AR_inr,
  input  AR_clr,
  input  PC_ld,
  input  PC_inr,
  input  PC_clr,
  input  [2:0] S3S2S1,
  input  DR_ld,
  input  DR_inr,
  input  DR_clr,
  input  C_in,
  input  AC_ld,
  input  AC_inr,
  input  lR,
  input  AC_clr,
  input  il,
  input  IR_ld,
  input  [2:0] SELC,
  input  TR_ld,
  input  TR_inr,
  input  TR_clr,
  input  comE,
  input  E_inp,
  input  DP_ld,
  input  DP_clr,
  input  clk,
  output [15:0] AR_opt,
  output [15:0] OUTpt,
  output [15:0] PC_opt,
  output [15:0] DR_opt,
  output [15:0] AC_opt,
  output [15:0] IR_opt,
  output [15:0] TR_opt
);

  wire alu_1_cout, e_ff_1_e_ff_opt;
  wire [11:0] ar_1_address;
  wire [15:0] alu_1_out_8, ram_1_dout;

  RAM #(.addrWidth(12), .asyncread("true"), .dataWidth(16)) ram_1 (
    .addr(ar_1_address), .we(write), .oe(out_ena), .clk(clk), .din(OUTpt), .dout(ram_1_dout));
  // Probe on alu_1_cout
  alu alu_1 (
    .cin(C_in), .Ac(AC_opt), .Dr(DR_opt), .S2S1S0(SELC), .ir(lR), .il(il), .cout(alu_1_cout),
    .out_8(alu_1_out_8));
  ir ir_1 (.inp(OUTpt), .ld(IR_ld), .clk(clk), .opt(IR_opt));  // open: clr
  ar ar_1 (.inp(OUTpt), .ld(AR_ld), .inr(AR_inr), .clr(AR_clr), .clk(clk), .address(ar_1_address), .opt(AR_opt));
  pc pc_1 (.inp(OUTpt), .ld(PC_ld), .inr(PC_inr), .clr(PC_clr), .clk(clk), .opt(PC_opt));
  dr dr_1 (.inp(OUTpt), .ld(DR_ld), .inr(DR_inr), .clr(DR_clr), .clk(clk), .opt(DR_opt));
  tr tr_1 (.inp(OUTpt), .ld(TR_ld), .inr(TR_inr), .clr(TR_clr), .clk(clk), .opt(TR_opt));
  // Probe on e_ff_1_e_ff_opt
  E_ff e_ff_1 (.comE(comE), .E_inp(E_inp), .ld(DP_ld), .clr(DP_clr), .clk(clk), .E_ff_opt(e_ff_1_e_ff_opt));
  ac ac_1 (.inp(alu_1_out_8), .ld(AC_ld), .inr(AC_inr), .clr(AC_clr), .clk(clk), .opt(AC_opt));
  Multiplexer #(.select(3), .width(16)) multiplexer_1 (
    .in1(AR_opt), .in2(PC_opt), .in3(DR_opt), .in4(AC_opt), .in5(IR_opt), .in6(TR_opt), .in7(ram_1_dout),
    .out(OUTpt), .sel(S3S2S1));  // open: in0
endmodule

module ac (
  input  [15:0] inp,
  input  ld,
  input  inr,
  input  clr,
  input  clk,
  output [15:0] opt
);

  wire [15:0] adder_1_out, multiplexer_1_out, multiplexer_2_out, multiplexer_3_out;

  Adder #(.width(16)) adder_1 (.a(opt), .b({16{1'b0}}), .out(adder_1_out), .cin(1'b1));  // open: cout
  Multiplexer #(.width(16)) multiplexer_1 (.in0(opt), .in1(adder_1_out), .out(multiplexer_1_out), .sel(inr));
  Multiplexer #(.width(16)) multiplexer_2 (.in0(multiplexer_1_out), .in1(inp), .out(multiplexer_2_out), .sel(ld));
  Register #(.width(16)) register_1 (.D(multiplexer_3_out), .clk(clk), .Q(opt));  // open: en, clr
  Multiplexer #(.width(16)) multiplexer_3 (
    .in0(multiplexer_2_out), .in1({16{1'b0}}), .out(multiplexer_3_out), .sel(clr));
endmodule

module ar (
  input  [15:0] inp,
  input  ld,
  input  inr,
  input  clr,
  input  clk,
  output [11:0] address,
  output [15:0] opt
);

  wire [11:0] adder_1_out, multiplexer_1_out, multiplexer_2_out, multiplexer_3_out;

  Adder #(.width(12)) adder_1 (.a(address), .b({12{1'b0}}), .out(adder_1_out), .cin(1'b1));  // open: cout
  Multiplexer #(.width(12)) multiplexer_1 (.in0(address), .in1(adder_1_out), .out(multiplexer_1_out), .sel(inr));
  Multiplexer #(.width(12)) multiplexer_2 (.in0(multiplexer_1_out), .in1(inp[11:0]), .out(multiplexer_2_out), .sel(ld));
  Register #(.width(12)) register_1 (.D(multiplexer_3_out), .clk(clk), .Q(address));  // open: en, clr
  Multiplexer #(.width(12)) multiplexer_3 (
    .in0(multiplexer_2_out), .in1({12{1'b0}}), .out(multiplexer_3_out), .sel(clr));

  assign opt = {4'b0000, address};

  // Other names for the same wires on the sheet: opt_t[11:0] = address
endmodule

module pc (
  input  [15:0] inp,
  input  ld,
  input  inr,
  input  clr,
  input  clk,
  output [15:0] opt
);

  wire [11:0] adder_1_out, multiplexer_1_out, multiplexer_2_out, multiplexer_3_out;

  Adder #(.width(12)) adder_1 (.a(opt[11:0]), .b({12{1'b0}}), .out(adder_1_out), .cin(1'b1));  // open: cout
  Multiplexer #(.width(12)) multiplexer_1 (.in0(opt[11:0]), .in1(adder_1_out), .out(multiplexer_1_out), .sel(inr));
  Multiplexer #(.width(12)) multiplexer_2 (.in0(multiplexer_1_out), .in1(inp[11:0]), .out(multiplexer_2_out), .sel(ld));
  Register #(.width(12)) register_1 (.D(multiplexer_3_out), .clk(clk), .Q(opt[11:0]));  // open: en, clr
  Multiplexer #(.width(12)) multiplexer_3 (
    .in0(multiplexer_2_out), .in1({12{1'b0}}), .out(multiplexer_3_out), .sel(clr));

  assign opt[15:12] = 4'b0000;

  // Other names for the same wires on the sheet: opt_t[11:0] = opt[11:0]
endmodule

module dr (
  input  [15:0] inp,
  input  ld,
  input  inr,
  input  clr,
  input  clk,
  output [15:0] opt
);

  wire [15:0] adder_1_out, multiplexer_1_out, multiplexer_2_out, multiplexer_3_out;

  Adder #(.width(16)) adder_1 (.a(opt), .b({16{1'b0}}), .out(adder_1_out), .cin(1'b1));  // open: cout
  Multiplexer #(.width(16)) multiplexer_1 (.in0(opt), .in1(adder_1_out), .out(multiplexer_1_out), .sel(inr));
  Multiplexer #(.width(16)) multiplexer_2 (.in0(multiplexer_1_out), .in1(inp), .out(multiplexer_2_out), .sel(ld));
  Register #(.width(16)) register_1 (.D(multiplexer_3_out), .clk(clk), .Q(opt));  // open: en, clr
  Multiplexer #(.width(16)) multiplexer_3 (
    .in0(multiplexer_2_out), .in1({16{1'b0}}), .out(multiplexer_3_out), .sel(clr));
endmodule

module ir (
  input  [15:0] inp,
  input  ld,
  input  clr,
  input  clk,
  output [15:0] opt
);

  wire [15:0] adder_1_out, multiplexer_1_out, multiplexer_2_out, multiplexer_3_out;

  Adder #(.width(16)) adder_1 (.a(opt), .b({16{1'b0}}), .out(adder_1_out), .cin(1'b1));  // open: cout
  Multiplexer #(.width(16)) multiplexer_1 (.in0(opt), .in1(adder_1_out), .out(multiplexer_1_out), .sel(1'b1));
  Multiplexer #(.width(16)) multiplexer_2 (.in0(multiplexer_1_out), .in1(inp), .out(multiplexer_2_out), .sel(ld));
  Register #(.width(16)) register_1 (.D(multiplexer_3_out), .clk(clk), .Q(opt));  // open: en, clr
  Multiplexer #(.width(16)) multiplexer_3 (
    .in0(multiplexer_2_out), .in1({16{1'b0}}), .out(multiplexer_3_out), .sel(clr));
endmodule

module tr (
  input  [15:0] inp,
  input  ld,
  input  inr,
  input  clr,
  input  clk,
  output [15:0] opt
);

  wire [15:0] adder_1_out, multiplexer_1_out, multiplexer_2_out, multiplexer_3_out;

  Adder #(.width(16)) adder_1 (.a(opt), .b({16{1'b0}}), .out(adder_1_out), .cin(1'b1));  // open: cout
  Multiplexer #(.width(16)) multiplexer_1 (.in0(opt), .in1(adder_1_out), .out(multiplexer_1_out), .sel(inr));
  Multiplexer #(.width(16)) multiplexer_2 (.in0(multiplexer_1_out), .in1(inp), .out(multiplexer_2_out), .sel(ld));
  Register #(.width(16)) register_1 (.D(multiplexer_3_out), .clk(clk), .Q(opt));  // open: en, clr
  Multiplexer #(.width(16)) multiplexer_3 (
    .in0(multiplexer_2_out), .in1({16{1'b0}}), .out(multiplexer_3_out), .sel(clr));
endmodule

module alu (
  input  cin,
  input  [15:0] Ac,
  input  [15:0] Dr,
  input  [2:0] S2S1S0,
  input  ir,
  input  il,
  output cout,
  output [15:0] out_8
);

  wire [15:0] adder_1_out, and_1_out, not_1_out;

  assign not_1_out = ~Ac;  // NOT_Gate not_1, 16 bits wide
  Adder #(.width(16)) adder_1 (.a(Ac), .b(Dr), .out(adder_1_out), .cin(cin), .cout(cout));
  assign and_1_out = Ac & Dr;  // AND_Gate and_1, 16 bits wide
  Multiplexer #(.select(3), .width(16)) multiplexer_1 (
    .in1(and_1_out), .in2(adder_1_out), .in3(Dr), .in5(not_1_out), .in6({ir, Ac[15:1]}),
    .in7({Ac[14:0], il}), .out(Ac), .sel(S2S1S0));  // open: in0, in4

  assign out_8 = Ac;
endmodule

module E_ff (
  input  comE,
  input  E_inp,
  input  ld,
  input  clr,
  input  clk,
  output E_ff_opt
);

  wire multiplexer_1_out, multiplexer_2_out, multiplexer_3_out, not_1_out;

  not not_1 (not_1_out, E_ff_opt);
  Multiplexer multiplexer_1 (.in0(E_ff_opt), .in1(not_1_out), .out(multiplexer_1_out), .sel(comE));
  Multiplexer multiplexer_2 (.in0(multiplexer_1_out), .in1(E_inp), .out(multiplexer_2_out), .sel(ld));
  Multiplexer multiplexer_3 (.in0(multiplexer_2_out), .in1(1'b0), .out(multiplexer_3_out), .sel(clr));
  D_Flip_Flop d_ff_1 (.D(multiplexer_3_out), .clk(clk), .Q(E_ff_opt));  // open: Qn, preset, reset
endmodule

module Sequence_counter (
  input  inr,
  input  clr,
  input  clk,
  output [3:0] seq_count
);

  wire [3:0] adder_1_out, multiplexer_1_out, multiplexer_2_out;

  Adder #(.width(4)) adder_1 (.a(seq_count), .b(4'b0001), .out(adder_1_out));  // open: cin, cout
  Multiplexer #(.width(4)) multiplexer_1 (.in0(seq_count), .in1(adder_1_out), .out(multiplexer_1_out), .sel(inr));
  Register #(.width(4)) register_1 (.D(multiplexer_2_out), .clk(clk), .Q(seq_count));  // open: en, clr
  Multiplexer #(.width(4)) multiplexer_2 (.in0(multiplexer_1_out), .in1(4'b0000), .out(multiplexer_2_out), .sel(clr));
endmodule

module Control_unit (
  input  SC_clr,
  input  [15:0] ir,
  input  SC_clk,
  input  R,
  input  E,
  input  [15:0] DR,
  input  [15:0] AC,
  output AR_ld,
  output AR_clr,
  output AR_inr,
  output PC_ld,
  output PC_inr,
  output PC_clr,
  output [2:0] S2S1S0,
  output DR_ld,
  output DR_inr,
  output DR_clr,
  output AC_ld,
  output AC_inr,
  output AC_clr,
  output IR_ld,
  output [2:0] selc
);

  wire and_1_out, and_2_out, and_3_out, and_4_out, and_5_out, and_6_out, and_7_out, and_8_out, and_9_out,
       and_10_out, and_11_out, and_12_out, and_15_out, and_16_out, and_18_out, and_19_out, and_20_out,
       and_21_out, and_22_out, and_23_out, and_24_out, and_25_out, and_28_out, and_29_out, and_30_out,
       and_31_out, and_32_out, and_33_out, and_35_out, and_36_out, and_37_out, and_38_out, D0, D1, D2, D3,
       D4, D5, D6, D7, not_1_out, not_2_out, not_3_out, not_4_out, not_5_out, not_6_out, not_7_out,
       not_8_out, not_9_out, or_1_out, or_2_out, or_6_out, or_7_out, or_13_out, or_15_out, or_21_out, T0, T1,
       T2, T3, T4, T5, T6, T7, T8, T9, T10, T11, T12, T13, T14, T15, X1, X2, X3, X4, X7;
  wire [3:0] sequence_counter_1_seq_count;

  not not_1 (not_1_out, R);
  not not_2 (not_2_out, D7);
  not not_3 (not_3_out, 1'b0);
  not not_4 (not_4_out, 1'b0);
  not not_5 (not_5_out, R);
  Sequence_counter sequence_counter_1 (
    .inr(1'b1), .clr(SC_clr), .clk(SC_clk), .seq_count(sequence_counter_1_seq_count));
  and and_1 (and_1_out, D4, T4);
  and and_2 (and_2_out, D5, T5);
  and and_3 (and_3_out, D5, T4);
  and and_4 (and_4_out, D0, T5);
  and and_5 (and_5_out, D1, T5);
  and and_6 (and_6_out, D2, T5);
  and and_7 (and_7_out, D0, T5);
  and and_8 (and_8_out, D1, T5);
  and and_9 (and_9_out, D3, T4);
  or or_1 (or_1_out, D0, D1, D2, D6);
  and and_10 (and_10_out, T0, not_1_out);
  and and_11 (and_11_out, not_1_out, T2);
  and and_12 (and_12_out, 1'b0, not_2_out, T3);
  and and_13 (AR_clr, T0, R);
  and and_14 (AR_inr, T4, D5);
  and and_15 (and_15_out, D7, not_3_out, T3);
  not not_6 (not_6_out, or_2_out);
  or or_2 (or_2_out, DR[15], DR[14], DR[13], DR[12], DR[11], DR[10], DR[9], DR[8], DR[6], DR[5], DR[4], DR[3], DR[2], DR[1], DR[0], DR[7]);
  or or_3 (S2S1S0[0], X1, X7, T2, X3);
  or or_4 (S2S1S0[1], X3, X7, X2, 1'b0);
  or or_5 (S2S1S0[2], T2, X7, 1'b0, X4);
  or or_6 (or_6_out, ir[6], ir[7], ir[9]);
  or or_7 (or_7_out, D0, D1, D2);
  and and_16 (and_16_out, D7, not_4_out, T3);
  and and_17 (IR_ld, not_5_out, T1);
  and and_18 (and_18_out, D1, T4);
  and and_19 (and_19_out, D0, T5);
  and and_20 (and_20_out, R, ir[7]);
  and and_21 (and_21_out, R, ir[9]);
  and and_22 (and_22_out, R, ir[6]);
  Decoder #(.enable("false"), .select(4)) decoder_1 (
    .out0(T0), .out1(T1), .out2(T2), .out3(T3), .out4(T4), .out5(T5), .out6(T6), .out7(T7), .out8(T8),
    .out9(T9), .out10(T10), .out11(T11), .out12(T12), .out13(T13), .out14(T14), .out15(T15),
    .sel(sequence_counter_1_seq_count));
  or or_8 (X1, and_1_out, and_2_out);
  or or_9 (X2, T0, and_3_out);
  or or_10 (X3, and_4_out, and_5_out, and_6_out);
  or or_11 (X4, and_7_out, and_8_out, and_9_out);
  and and_23 (and_23_out, or_1_out, T4);
  or or_12 (AR_ld, and_10_out, and_11_out, and_12_out);
  or or_13 (or_13_out, D0, D1, D2, D6);
  and and_24 (and_24_out, or_7_out, T5);
  and and_25 (and_25_out, or_6_out, and_16_out);
  or or_14 (X7, T1, and_23_out, R);
  not not_7 (not_7_out, AC[15]);
  not not_8 (not_8_out, or_15_out);
  or or_15 (or_15_out, AC[15], AC[14], AC[13], AC[12], AC[11], AC[10], AC[9], AC[8], AC[6], AC[5], AC[4], AC[3], AC[2], AC[1], AC[0], AC[7]);
  and and_26 (DR_ld, or_13_out, T4);
  and and_27 (DR_inr, D6, T5);
  or or_16 (AC_ld, and_24_out, and_25_out);
  and and_28 (and_28_out, D2, T4);
  and and_29 (and_29_out, ir[1], not_9_out);
  and and_30 (and_30_out, ir[2], not_8_out);
  and and_31 (and_31_out, ir[3], AC[15]);
  and and_32 (and_32_out, ir[4], not_7_out);
  or or_17 (selc[0], and_18_out, and_21_out, and_20_out);
  or or_18 (selc[1], and_21_out, and_19_out);
  or or_19 (selc[2], and_19_out, and_22_out);
  and and_33 (and_33_out, D4, T4);
  not not_9 (not_9_out, E);
  and and_34 (AC_inr, ir[5], and_16_out);
  and and_35 (and_35_out, ir[11], and_16_out);
  or or_20 (AC_clr, and_35_out, and_28_out);
  or or_21 (or_21_out, and_29_out, and_30_out, and_31_out, and_32_out);
  and and_36 (and_36_out, D5, T5);
  and and_37 (and_37_out, or_21_out, and_15_out);
  and and_38 (and_38_out, not_6_out, D6, T6);
  or or_22 (PC_ld, and_33_out, and_36_out);
  or or_23 (PC_inr, and_37_out, and_38_out, T1);
  Decoder #(.enable("false"), .select(3)) decoder_2 (
    .out0(D0), .out1(D1), .out2(D2), .out3(D3), .out4(D4), .out5(D5), .out6(D6), .out7(D7), .sel(ir[14:12]));

  assign DR_clr = 1'b0;
  assign PC_clr = 1'b0;

  // Other names for the same wires on the sheet: B0 = ir[0]; B1 = ir[1]; B2 = ir[2]; B3 = ir[3]; B4 = ir[4];
  //   B5 = ir[5]; B6 = ir[6]; B7 = ir[7]; B8 = ir[8]; B9 = ir[9]; B10 = ir[10]; B11 = ir[11]; l = ir[15];
  //   S0 = S2S1S0[0]; S1 = S2S1S0[1]; S2 = S2S1S0[2]; X5 = T2
endmodule
